# Fritzing sketch blip (saved by Fritzing 0.9.2b)
breadboards: 1

parts:
  R4 = Resistor [tolerance=±5% resistance=560 package=THT]
  LED1 = LED - 5mm [color="Red (633nm)" package="5 mm [THT]"]
  Part3 = Photon

nets:
  N1: R4.Pin_0, LED1.cathode
  N2: R4.Pin_1, Part3.GND
  N3: LED1.anode, Part3.D0
