# Fritzing sketch bpm-085 (saved by Fritzing 0.9.2b)
breadboards: 1

parts:
  Part3 = Barometric Pressure Sensor - BMP085 Breakout
  Part4 = Photon

nets:
  VCC: Part3.VCC, Part4.3V3
  GND: Part3.GND, Part4.GND
  N1: Part3.SCL, Part4.D1
  N2: Part3.SDA, Part4.D0
