# Fritzing sketch light-sensor (saved by Fritzing 0.9.2b)
breadboards: 1

parts:
  R1 = Photocell (LDR) [package=THT]
  R2 = Resistor [tolerance=±5% resistance=560 package=THT]
  Part1 = Photon

nets:
  N1: R1.pin_0, R2.Pin_0, Part1.A0
  N2: R1.pin_1, Part1.3V3
  N3: R2.Pin_1, Part1.GND
