# Fritzing sketch shift-register (saved by Fritzing 0.9.2b)
breadboards: 1

parts:
  U1 = 74HC595 [package="DIP16 [THT]"]
  R1 = Resistor [tolerance=±5% resistance=560 package=THT]
  R2 = Resistor [tolerance=±5% resistance=560 package=THT]
  R3 = Resistor [tolerance=±5% resistance=560 package=THT]
  R4 = Resistor [tolerance=±5% resistance=560 package=THT]
  LED1 = LED - 5mm [color="Red (633nm)" package="5 mm [THT]"]
  LED2 = LED - 5mm [color="Red (633nm)" package="5 mm [THT]"]
  LED3 = LED - 5mm [color="Red (633nm)" package="5 mm [THT]"]
  LED4 = LED - 5mm [color="Red (633nm)" package="5 mm [THT]"]
  Part1 = Photon

nets:
  N1: U1.Q2, LED1.anode
  N2: U1.Q3, LED2.anode
  N3: U1.Q4, LED3.anode
  N4: U1.Q5, LED4.anode
  GND: U1.GND, U1.OE, R1.Pin_1, R2.Pin_1, R3.Pin_1, R4.Pin_1, Part1.GND
  VCC: U1.MR, U1.VCC, Part1.3V3
  N5: U1.SH_CP, Part1.A3
  N6: U1.ST_CP, Part1.A2
  N7: U1.DS, Part1.A5
  N8: R1.Pin_0, LED1.cathode
  N9: R2.Pin_0, LED4.cathode
  N10: R3.Pin_0, LED3.cathode
  N11: R4.Pin_0, LED2.cathode
